# Fritzing sketch weather_station_schem (saved by Fritzing 0.9.10b)
breadboards: 1

parts:
  MCU = Heltec WiFi LoRa 32 V3 [part_number=HTIT-WB32LA]
  Wind_Speed_&_Heading = RJ9 [package=rj9]
  Rainfall = RJ9 [package=rj9]
  Part1 = BME280 Breakout
  R1 = Resistor [tolerance=±5% power=0.25 resistance=10k package=THT]
  R2 = Resistor [tolerance=±5% power=0.25 resistance=10k package=THT]
  R3 = Resistor [tolerance=±5% power=0.25 resistance=10k package=THT]
  R4 = Resistor [tolerance=±5% power=0.25 resistance=680 package=THT]
  R5 = Resistor [tolerance=±5% power=0.25 resistance=680 package=THT]
  C1 = Electrolytic Capacitor [capacitance=4.7µF voltage=50V package="100 mil [THT, electrolytic]"]
  C2 = Electrolytic Capacitor [capacitance=4.7µF voltage=50V package="100 mil [THT, electrolytic]"]
  C3 = Ceramic Capacitor [capacitance=100nF voltage=50V package="100 mil [THT, multilayer]"]

nets:
  N1: MCU.pin_3, Rainfall.3, R3.Pin_1, R4.Pin_0
  N2: MCU.pin_4, Wind_Speed_&_Heading.3, R2.Pin_1, R5.Pin_0
  N3: MCU.pin_6, Wind_Speed_&_Heading.4, R1.Pin_1, C3.1
  N4: MCU.pin_9, Part1.SDI/SDA
  N5: MCU.pin_10, Part1.SCK/SCL
  3.3V: MCU.pin_16, MCU.pin_17, Part1.3.3V, R1.Pin_0, R2.Pin_0, R3.Pin_0
  GND: MCU.pin_18, MCU.pin_19, Wind_Speed_&_Heading.1, Wind_Speed_&_Heading.2, Rainfall.2, Part1.GND, C1.-, C2.-, C3.0
  N6: MCU.pin_21, MCU.pin_22
  NC: Part1.!CS, Part1.SDO/ADR
  N7: R4.Pin_1, C2.+
  N8: R5.Pin_1, C1.+

notes:
  LoRa ESP32 Weather Station, Outdoor sensors and MCU, 1
  R. Galeoto (Bitrot_alpha) 2023

custom parts:
  Heltec WiFi LoRa 32 V3: The Heltec WiFi LoRa 32 is an IoT development board designed and produced by Heltec Automation and based on the Espressif ESP32-S3FN8 and Semtech SX1262 modules. The board includes WiFi, Bluetooth and LoRa functions, as well as a 0.96″ OLED display and a lithium battery management system. Links: Heltec WiFi LoRa 32 product page Github
